# Fritzing sketch circuit_test (saved by Fritzing 0.9.6b)
breadboards: 1

parts:
  Part4 = Arduino Nano (Rev3.0)
  Part5 = I2C level shifter bidirectional
  Mod2 = Raspberry Pi 4B

nets:
  N1: Part4.D2, Part5.HV2
  N2: Part4.D4, Part5.HV1
  GND: Part5.GND, Mod2.GND
  N3: Part5.LV, Mod2.3V3
  N4: Part5.LV2, Mod2.GPIO21
  N5: Part5.LV1, Mod2.GPIO20
  N6: Part5.HV, Mod2.5V
